// Logisim project Datapath_ver1 - Copy.circ as structural Verilog: 10 circuits, main circuit ALU 8 bit
module ALU_8_bit (
  input  Cin,
  input  [7:0] Operand_A,
  input  [7:0] Operand_B,
  input  [2:0] ALUop,
  input  Binvert,
  output ZeroFlag,
  output [7:0] Result,
  output Overflow
);

  wire [7:0] adder_1_out, bit_extender_1_out, multiplexer_1_out, not_1_out;

  assign not_1_out = ~Operand_B;  // NOT_Gate not_1, 8 bits wide
  Multiplexer #(.width(8), .enable("false")) multiplexer_1 (
    .in0(Operand_B), .in1(not_1_out), .out(multiplexer_1_out), .sel(Binvert));
  assign bit_extender_1_out = {{7{1'b0}}, adder_1_out[7]};  // Bit_Extender bit_extender_1
  Adder adder_1 (.a(Operand_A), .b(multiplexer_1_out), .out(adder_1_out), .cin(Cin), .cout(Overflow));
  nor nor_1 (ZeroFlag, Result[7], Result[6], Result[5], Result[4], Result[3], Result[2], Result[1], Result[0]);
  Multiplexer #(.select(3), .width(8), .enable("false")) multiplexer_2 (
    .in0(adder_1_out), .in1(adder_1_out), .in2(bit_extender_1_out), .in3(adder_1_out), .in4(adder_1_out),
    .in5(adder_1_out), .in6(adder_1_out), .in7(adder_1_out), .out(Result), .sel(ALUop));

  // Notes on the sheet:
  //   SLT
endmodule

module Register_File (
  input  RegWrite,
  input  [7:0] Write_Data_in,
  input  [1:0] RS,
  input  CLock,
  input  [1:0] RD,
  output [7:0] DATA01,
  output [7:0] DATA02
);

  wire and_1_out, and_2_out, and_3_out, and_4_out, decoder_1_out0, decoder_1_out1, decoder_1_out2,
       decoder_1_out3;
  wire [7:0] register_1_q, register_2_q, register_3_q, register_4_q;

  Decoder #(.select(2), .enable("false")) decoder_1 (
    .out0(decoder_1_out0), .out1(decoder_1_out1), .out2(decoder_1_out2), .out3(decoder_1_out3), .sel(RD));
  and and_1 (and_1_out, RegWrite, decoder_1_out0);
  and and_2 (and_2_out, RegWrite, decoder_1_out1);
  and and_3 (and_3_out, RegWrite, decoder_1_out2);
  and and_4 (and_4_out, RegWrite, decoder_1_out3);
  Register register_1 (.D(Write_Data_in), .en(and_1_out), .Q(register_1_q), .clk(CLock));  // open: clr
  Register register_2 (.D(Write_Data_in), .en(and_2_out), .Q(register_2_q), .clk(CLock));  // open: clr
  Register register_3 (.D(Write_Data_in), .en(and_3_out), .Q(register_3_q), .clk(CLock));  // open: clr
  Register register_4 (.D(Write_Data_in), .en(and_4_out), .Q(register_4_q), .clk(CLock));  // open: clr
  Multiplexer #(.select(2), .width(8), .enable("false")) multiplexer_1 (
    .in0(register_1_q), .in1(register_2_q), .in2(register_3_q), .in3(register_4_q), .out(DATA01), .sel(RS));
  Multiplexer #(.select(2), .width(8), .enable("false")) multiplexer_2 (
    .in0(register_1_q), .in1(register_2_q), .in2(register_3_q), .in3(register_4_q), .out(DATA02), .sel(RD));

  // Notes on the sheet:
  //   ACC
  //   S1
  //   S2
  //   t1
endmodule

module Main_control_unit_KMAP (
  input  [2:0] Ins_Input,
  output ALUsrc,
  output MemtoReg,
  output RegWrite,
  output MemRead,
  output MemWrite,
  output BranchBNE,
  output ACC_CU,
  output Display,
  output Binvert,
  output [2:0] aluopextra
);

  wire and_5_out, and_6_out, and_7_out, and_8_out, and_10_out, and_11_out, and_12_out, and_13_out,
       and_14_out, not_1_out, not_2_out, not_3_out;
  wire [2:2] or_1_out;

  not not_1 (not_1_out, Ins_Input[2]);
  not not_2 (not_2_out, Ins_Input[0]);
  not not_3 (not_3_out, Ins_Input[1]);
  and and_1 (MemtoReg, Ins_Input[2], not_3_out);
  and and_2 (MemRead, Ins_Input[2], not_3_out, not_2_out);
  and and_3 (MemWrite, Ins_Input[2], not_3_out, Ins_Input[0]);
  and and_4 (BranchBNE, not_1_out, Ins_Input[1], Ins_Input[0]);
  and and_5 (and_5_out, not_1_out, Ins_Input[0]);
  and and_6 (and_6_out, not_1_out, Ins_Input[1]);
  and and_7 (and_7_out, not_1_out, Ins_Input[0]);
  and and_8 (and_8_out, not_1_out, Ins_Input[1]);
  and and_9 (aluopextra[1], Ins_Input[2], Ins_Input[1], Ins_Input[0]);
  and and_10 (and_10_out, Ins_Input[2], not_3_out);
  and and_11 (and_11_out, not_1_out, Ins_Input[1], Ins_Input[0]);
  and and_12 (and_12_out, Ins_Input[2], not_2_out);
  and and_13 (and_13_out, not_1_out, Ins_Input[1], Ins_Input[0]);
  or or_1 (or_1_out[2], and_5_out, and_6_out);
  or or_2 (Binvert, and_7_out, and_8_out);
  and and_14 (and_14_out, Ins_Input[2], not_3_out);
  and and_15 (Display, Ins_Input[2], Ins_Input[1], Ins_Input[0]);
  or or_3 (ALUsrc, and_10_out, and_11_out, and_12_out);
  or or_4 (aluopextra[2], or_1_out[2], aluopextra[1]);
  or or_5 (RegWrite, not_2_out, and_13_out);
  or or_6 (ACC_CU, and_14_out, and_13_out);

  assign aluopextra[0] = aluopextra[1];

  // Notes on the sheet:
  //   A    B   C
  //   0
  //   2
  //   1
  //   B
  //   A
  //   A'
  //   3
  //   4
  //   C
  //   C'
  //   B'
endmodule

module datapath (
  input  [1:0] ACC,
  input  [7:0] in_2,
  output [7:0] out_3,
  output [7:0] out_4,
  output [7:0] out_5,
  output Shamt,
  output [1:0] RS,
  output [1:0] RD,
  output [2:0] OP,
  output [7:0] out_10,
  output [7:0] out_11,
  output [7:0] out_12,
  output [7:0] out_13,
  output [7:0] out_14,
  output [7:0] out_15,
  output [2:0] out_16,
  output [7:0] out_17,
  output [2:0] out_18
);

  wire alu_8_bit_1_overflow, alu_8_bit_1_zeroflag, blockbottom2_1_out_3, blockbottom2_1_out_4,
       blockbottom2_1_out_5, blockbottom2_1_out_6, blockbottom2_1_out_7, blockbottom2_1_out_8,
       blockbottom2_1_out_9, blockbottom2_1_out_10, blocktop2_1_out_3, blocktop2_1_out_4, blocktop2_1_out_5,
       blocktop2_1_out_6, blocktop2_1_out_7, blocktop2_1_out_8, blocktop2_1_out_9, blocktop2_1_out_10,
       branch_circuit_1_out_2, clock_1_out, main_control_unit_kmap_1_acc_cu, main_control_unit_kmap_1_alusrc,
       main_control_unit_kmap_1_binvert, main_control_unit_kmap_1_branchbne,
       main_control_unit_kmap_1_display, main_control_unit_kmap_1_memread, main_control_unit_kmap_1_memtoreg,
       main_control_unit_kmap_1_memwrite, main_control_unit_kmap_1_regwrite;
  wire [1:0] multiplexer_2_out;
  wire [2:0] main_control_unit_kmap_1_aluopextra;
  wire [7:0] bit_extender_2_out, bit_extender_3_out, blackbox_1_out_3, blackbox_1_out_4, multiplexer_3_out,
       ram_1_data, shifter_1_out;

  Register PC (.D(out_3), .Q(out_10), .clk(clock_1_out));  // open: en, clr
  Clock clock_1 (.out(clock_1_out));
  Multiplexer #(.width(8), .enable("false")) multiplexer_1 (
    .in0(out_4), .in1(out_5), .out(out_3), .sel(branch_circuit_1_out_2));
  Adder adder_1 (.a(8'h1), .b(out_10), .out(out_4));  // open: cin, cout
  ROM rom_1 (.addr(out_10), .data({OP, RD, out_16}));  // open: sel
  branch_circuit branch_circuit_1 (.branch_CU_line(main_control_unit_kmap_1_branchbne), .out_2(branch_circuit_1_out_2));
  Multiplexer #(.width(2), .enable("false")) multiplexer_2 (
    .in0(out_16[2:1]), .in1(ACC), .out(multiplexer_2_out), .sel(main_control_unit_kmap_1_acc_cu));
  Main_control_unit_KMAP main_control_unit_kmap_1 (
    .Ins_Input(OP), .MemtoReg(main_control_unit_kmap_1_memtoreg),
    .RegWrite(main_control_unit_kmap_1_regwrite), .MemWrite(main_control_unit_kmap_1_memwrite),
    .BranchBNE(main_control_unit_kmap_1_branchbne), .Binvert(main_control_unit_kmap_1_binvert),
    .MemRead(main_control_unit_kmap_1_memread), .ALUsrc(main_control_unit_kmap_1_alusrc),
    .ACC_CU(main_control_unit_kmap_1_acc_cu), .Display(main_control_unit_kmap_1_display),
    .aluopextra(main_control_unit_kmap_1_aluopextra));
  Register_File register_file_1 (
    .Write_Data_in(out_14), .DATA01(out_12), .RD(RD), .RS(multiplexer_2_out),
    .RegWrite(main_control_unit_kmap_1_regwrite), .DATA02(out_15), .CLock(clock_1_out));
  assign out_17 = {{5{1'b0}}, out_16};  // Bit_Extender bit_extender_1
  Shifter shifter_1 (.in(out_17), .\dist (3'b001), .out(shifter_1_out));
  ALU_8_bit alu_8_bit_1 (
    .Operand_A(out_12), .Operand_B(multiplexer_3_out), .Binvert(main_control_unit_kmap_1_binvert),
    .Cin(main_control_unit_kmap_1_binvert), .ALUop(main_control_unit_kmap_1_aluopextra),
    .Overflow(alu_8_bit_1_overflow), .Result(out_13), .ZeroFlag(alu_8_bit_1_zeroflag));
  Multiplexer #(.width(8), .enable("false")) multiplexer_3 (
    .in0(out_15), .in1(out_17), .out(multiplexer_3_out), .sel(main_control_unit_kmap_1_alusrc));
  Adder adder_2 (.a(out_4), .b(shifter_1_out), .out(out_5));  // open: cin, cout
  RAM #(.bus("separate")) ram_1 (
    .addr(out_13), .din(out_15), .data(ram_1_data), .str(main_control_unit_kmap_1_memwrite),
    .clk(clock_1_out), .ld(main_control_unit_kmap_1_memread));  // open: sel, clr
  assign bit_extender_2_out = {{4{1'b0}}, out_11[7:4]};  // Bit_Extender bit_extender_2
  blocktop2 blocktop2_1 (
    .in_2(blackbox_1_out_3), .in_1(blackbox_1_out_4), .out_8(blocktop2_1_out_8), .out_10(blocktop2_1_out_10),
    .out_6(blocktop2_1_out_6), .out_4(blocktop2_1_out_4), .out_7(blocktop2_1_out_7),
    .out_9(blocktop2_1_out_9), .out_5(blocktop2_1_out_5), .out_3(blocktop2_1_out_3));
  _7_Segment_Display u_7_segment_display_1 (
    .g(blocktop2_1_out_8), .f(blocktop2_1_out_10), .a(blocktop2_1_out_6), .b(blocktop2_1_out_4),
    .e(blockbottom2_1_out_9), .d(blockbottom2_1_out_3), .c(blockbottom2_1_out_4), .dp(blockbottom2_1_out_5));
  blockbottom2 blockbottom2_1 (
    .out_9(blockbottom2_1_out_9), .out_3(blockbottom2_1_out_3), .out_4(blockbottom2_1_out_4),
    .out_5(blockbottom2_1_out_5), .out_10(blockbottom2_1_out_10), .out_6(blockbottom2_1_out_6),
    .out_7(blockbottom2_1_out_7), .out_8(blockbottom2_1_out_8), .in_1(blackbox_1_out_3),
    .in_2(blackbox_1_out_4));
  blackbox blackbox_1 (
    .out_3(blackbox_1_out_3), .out_4(blackbox_1_out_4), .in_1(bit_extender_2_out), .in_2(bit_extender_3_out));
  Multiplexer #(.width(8), .enable("false")) multiplexer_4 (
    .in0(in_2), .in1(out_14), .out(out_11), .sel(main_control_unit_kmap_1_display));
  Multiplexer #(.width(8), .enable("false")) multiplexer_5 (
    .in0(out_13), .in1(ram_1_data), .out(out_14), .sel(main_control_unit_kmap_1_memtoreg));
  _7_Segment_Display u_7_segment_display_2 (
    .g(blocktop2_1_out_7), .f(blocktop2_1_out_9), .a(blocktop2_1_out_5), .b(blocktop2_1_out_3),
    .e(blockbottom2_1_out_10), .d(blockbottom2_1_out_6), .c(blockbottom2_1_out_7), .dp(blockbottom2_1_out_8));
  assign bit_extender_3_out = {{4{1'b0}}, out_11[3:0]};  // Bit_Extender bit_extender_3
  LED overflow (.in(alu_8_bit_1_overflow));

  assign out_18 = OP;
  assign RS = out_16[2:1];
  assign Shamt = out_16[0];

  // Notes on the sheet:
  //   contents of rom_1 (hex, n*v repeats v):
  //   20 c1 8a 94 20 4 68 8 28 20 c1 ae
endmodule

module branch_circuit (
  input  branch_CU_line,
  output out_2
);

  and and_1 (out_2, branch_CU_line, 1'b1);
endmodule

module blocktop2 (
  input  [7:0] in_1,
  input  [7:0] in_2,
  output out_3,
  output out_4,
  output out_5,
  output out_6,
  output out_7,
  output out_8,
  output out_9,
  output out_10
);

  convertertop convertertop_1 (.in_1(in_2), .out_2(out_8), .out_3(out_10), .out_4(out_6), .out_5(out_4));
  convertertop convertertop_2 (.in_1(in_1), .out_2(out_7), .out_3(out_9), .out_4(out_5), .out_5(out_3));
endmodule

module blockbottom2 (
  input  [7:0] in_1,
  input  [7:0] in_2,
  output out_3,
  output out_4,
  output out_5,
  output out_6,
  output out_7,
  output out_8,
  output out_9,
  output out_10
);

  converter_bottom converter_bottom_1 (.in_1(in_1), .out_2(out_9), .out_3(out_3), .out_4(out_4), .out_5(out_5));
  converter_bottom converter_bottom_2 (.in_1(in_2), .out_2(out_10), .out_3(out_6), .out_4(out_7), .out_5(out_8));
endmodule

module blackbox (
  input  [7:0] in_1,
  input  [7:0] in_2,
  output [7:0] out_3,
  output [7:0] out_4
);


  assign out_3 = in_1;
  assign out_4 = in_2;
endmodule

module convertertop (
  input  [7:0] in_1,
  output out_2,
  output out_3,
  output out_4,
  output out_5
);

  wire and_1_out, or_1_out;
  wire [7:0] multiplexer_1_out, multiplexer_2_out;
  wire [7:4] multiplexer_3_out;

  Multiplexer #(.select(4), .width(8), .enable("false")) multiplexer_1 (
    .in0(8'h77), .in1(8'h41), .in2(8'h3b), .in3(8'h6b), .in4(8'h4d), .in5(8'h6e), .in6(8'h7e), .in7(8'h43),
    .in8(8'h7f), .in9(8'h6f), .in10(8'h5f), .in11(8'h7c), .in12(8'h36), .in13(8'h79), .in14(8'h3e),
    .in15(8'h1e), .out(multiplexer_1_out), .sel(in_1[3:0]));
  or or_1 (or_1_out, in_1[4], in_1[5], in_1[6], in_1[7]);
  Multiplexer #(.width(8), .enable("false")) multiplexer_2 (
    .in0(multiplexer_1_out), .in1(8'h9b), .out(multiplexer_2_out), .sel(or_1_out));
  and and_1 (and_1_out, in_1[0], in_1[1], in_1[2], in_1[3], in_1[4], in_1[5], in_1[6], in_1[7]);
  Multiplexer #(.width(8), .enable("false")) multiplexer_3 (
    .in0(multiplexer_2_out), .in1({8{1'b0}}), .out({multiplexer_3_out, out_2, out_3, out_4, out_5}),
    .sel(and_1_out));

  // Notes on the sheet:
  //   0
  //   1
  //   2
  //   3
  //   4
  //   5
  //   6
  //   7
  //   8
  //   9
  //   a
  //   b
  //   c
  //   d
  //   e
  //   f
  //   ?
endmodule

module converter_bottom (
  input  [7:0] in_1,
  output out_2,
  output out_3,
  output out_4,
  output out_5
);

  wire and_1_out, or_1_out;
  wire [3:0] multiplexer_3_out;
  wire [7:0] multiplexer_1_out, multiplexer_2_out;

  Multiplexer #(.select(4), .width(8), .enable("false")) multiplexer_1 (
    .in0(8'h77), .in1(8'h41), .in2(8'h3b), .in3(8'h6b), .in4(8'h4d), .in5(8'h6e), .in6(8'h7e), .in7(8'h43),
    .in8(8'h7f), .in9(8'h6f), .in10(8'h5f), .in11(8'h7c), .in12(8'h36), .in13(8'h79), .in14(8'h3e),
    .in15(8'h1e), .out(multiplexer_1_out), .sel(in_1[3:0]));
  or or_1 (or_1_out, in_1[4], in_1[5], in_1[6], in_1[7]);
  Multiplexer #(.width(8), .enable("false")) multiplexer_2 (
    .in0(multiplexer_1_out), .in1(8'h9b), .out(multiplexer_2_out), .sel(or_1_out));
  and and_1 (and_1_out, in_1[0], in_1[1], in_1[2], in_1[3], in_1[4], in_1[5], in_1[6], in_1[7]);
  Multiplexer #(.width(8), .enable("false")) multiplexer_3 (
    .in0(multiplexer_2_out), .in1({8{1'b0}}), .out({out_5, out_4, out_3, out_2, multiplexer_3_out}),
    .sel(and_1_out));

  // Notes on the sheet:
  //   0
  //   1
  //   2
  //   3
  //   4
  //   5
  //   6
  //   7
  //   8
  //   9
  //   a
  //   b
  //   c
  //   d
  //   e
  //   f
  //   ?
endmodule
